# Fritzing sketch body (saved by Fritzing 0.9.6b)
circuit board: 3.33311cm x 4.48589cm
breadboards: 1

parts:
  ProMini = Arduino Pro Mini v13
  D2 = Dagu DGServo 9g header (male) [package=THT]
  D6 = Dagu DGServo 9g header (male) [package=THT]
  D11 = Dagu DGServo 9g header (male) [package=THT]
  D9 = Dagu DGServo 9g header (male) [package=THT]
  D10 = Dagu DGServo 9g header (male) [package=THT]
  R1 = Resistor [tolerance=±2% power=0.25 resistance=330 package=THT]
  A0 = Resistor [tolerance=±2% power=0.25 resistance=330 package=THT]
  5v+ = female pin header, 2 pins [form="♀ (female)"]
  D3 = Dagu DGServo 9g header (male) [package=THT]
  D4 = Dagu DGServo 9g header (male) [package=THT]
  D5 = Dagu DGServo 9g header (male) [package=THT]
  D7 = Dagu DGServo 9g header (male) [package=THT]
  D8 = Dagu DGServo 9g header (male) [package=THT]

nets:
  N1: ProMini.A0, R1.Pin_1, A0.Pin_1
  N2: ProMini.D11_PWM/MOSI, D11.pulse
  N3: ProMini.D10_PWM/SS, D10.pulse
  N4: ProMini.D9_PWM, D9.pulse
  N5: ProMini.D8, D8.pulse
  N6: ProMini.D7, D7.pulse
  N7: ProMini.D6_PWM, D6.pulse
  N8: ProMini.D5_PWM, D5.pulse
  N9: ProMini.D4, D4.pulse
  N10: ProMini.D3_PWM, D3.pulse
  N11: ProMini.D2, D2.pulse
  GND: D2.gnd, D6.gnd, D11.gnd, D9.gnd, D10.gnd, R1.Pin_0, 5v+.pin2, D3.gnd, D4.gnd, D5.gnd, D7.gnd, D8.gnd
  VCC: D2.Vcc, D6.Vcc, D11.Vcc, D9.Vcc, D10.Vcc, A0.Pin_0, 5v+.pin1, D3.Vcc, D4.Vcc, D5.Vcc, D7.Vcc, D8.Vcc
